// Digital circuit D0.dig as structural Verilog
module D0 (
  input  X0,
  input  X1,
  input  X2,
  input  Q0,
  output D0
);

  wire and_1_out, and_2_out, and_3_out, and_4_out, not_1_out, not_2_out, not_3_out, not_4_out;

  not not_1 (not_1_out, X0);
  not not_2 (not_2_out, X1);
  not not_3 (not_3_out, X2);
  not not_4 (not_4_out, Q0);
  and and_1 (and_1_out, X0, X1, not_3_out);
  and and_2 (and_2_out, X1, Q0);
  and and_3 (and_3_out, Q0, X0);
  and and_4 (and_4_out, not_3_out, Q0);
  or or_1 (D0, and_1_out, and_2_out, and_3_out, and_4_out);
endmodule

/* Test case:
Q0	X2	X1	X0	D0			
0	0	0	0	0
0	0	0	1	0
0	0	1	0	0
0	0	1	1	1
0	1	0	0	0
0	1	0	1	0
0	1	1	0	0
0	1	1	1	0
1	0	0	0	1
1	0	0	1	1
1	0	1	0	1
1	0	1	1	1
1	1	0	0	0
1	1	0	1	1
1	1	1	0	1
1	1	1	1	1
0	0	0	0	0
0	0	0	1	0
0	0	1	0	0
0	0	1	1	1
0	1	0	0	0
0	1	0	1	0
0	1	1	0	0
0	1	1	1	0
1	0	0	0	1
1	0	0	1	1
1	0	1	0	1
1	0	1	1	1
1	1	0	0	0
1	1	0	1	1
1	1	1	0	1
1	1	1	1	1
0	0	0	0	0
0	0	0	1	0
0	0	1	0	0
0	0	1	1	1
0	1	0	0	0
0	1	0	1	0
0	1	1	0	0
0	1	1	1	0
1	0	0	0	1
1	0	0	1	1
1	0	1	0	1
1	0	1	1	1
1	1	0	0	0
1	1	0	1	1
1	1	1	0	1
1	1	1	1	1
0	0	0	0	X
0	0	0	1	X
0	0	1	0	X
0	0	1	1	X
0	1	0	0	X
0	1	0	1	X
0	1	1	0	X
0	1	1	1	X
1	0	0	0	X
1	0	0	1	X
1	0	1	0	X
1	0	1	1	X
1	1	0	0	X
1	1	0	1	X
1	1	1	0	X
1	1	1	1	X
*/
