// Digital circuit Motor.dig as structural Verilog
module Motor (
  input  X0,
  input  X1,
  input  X2,
  input  Q0,
  input  Q1,
  input  Q2,
  output M
);

  wire and_1_out, and_2_out, and_3_out, and_4_out, not_1_out, not_2_out, not_3_out, not_4_out, not_5_out,
       not_6_out;

  or or_1 (M, and_4_out, and_3_out, and_2_out, and_1_out);
  and and_1 (and_1_out, not_2_out, X0, not_3_out, not_5_out);
  and and_2 (and_2_out, not_3_out, Q1, not_1_out);
  and and_3 (and_3_out, Q2, not_2_out, not_3_out);
  and and_4 (and_4_out, not_6_out, not_3_out, not_1_out, X1);
  not not_1 (not_1_out, X0);
  not not_2 (not_2_out, X1);
  not not_3 (not_3_out, X2);
  not not_4 (not_4_out, Q0);
  not not_5 (not_5_out, Q1);
  not not_6 (not_6_out, Q2);
endmodule

/* Test case:
Q2	Q1	Q0	X2	X1	X0	M	
0	0	0	0	0	0	0
0	0	0	0	0	1	1
0	0	0	0	1	0	1
0	0	0	0	1	1	0
0	0	0	1	0	0	0
0	0	0	1	0	1	0
0	0	0	1	1	0	0
0	0	0	1	1	1	0
0	0	1	0	0	0	0
0	0	1	0	0	1	1
0	0	1	0	1	0	1
0	0	1	0	1	1	0
0	0	1	1	0	0	0
0	0	1	1	0	1	0
0	0	1	1	1	0	0
0	0	1	1	1	1	0
0	1	0	0	0	0	1
0	1	0	0	0	1	0
0	1	0	0	1	0	1
0	1	0	0	1	1	0
0	1	0	1	0	0	0
0	1	0	1	0	1	0
0	1	0	1	1	0	0
0	1	0	1	1	1	0
0	1	1	0	0	0	1
0	1	1	0	0	1	0
0	1	1	0	1	0	1
0	1	1	0	1	1	0
0	1	1	1	0	0	0
0	1	1	1	0	1	0
0	1	1	1	1	0	0
0	1	1	1	1	1	0
1	0	0	0	0	0	1
1	0	0	0	0	1	1
1	0	0	0	1	0	0
1	0	0	0	1	1	0
1	0	0	1	0	0	0
1	0	0	1	0	1	0
1	0	0	1	1	0	0
1	0	0	1	1	1	0
1	0	1	0	0	0	1
1	0	1	0	0	1	1
1	0	1	0	1	0	0
1	0	1	0	1	1	0
1	0	1	1	0	0	0
1	0	1	1	0	1	0
1	0	1	1	1	0	0
1	0	1	1	1	1	0
1	1	0	0	0	0	X
1	1	0	0	0	1	X
1	1	0	0	1	0	X
1	1	0	0	1	1	X
1	1	0	1	0	0	X
1	1	0	1	0	1	X
1	1	0	1	1	0	X
1	1	0	1	1	1	X
1	1	1	0	0	0	X
1	1	1	0	0	1	X
1	1	1	0	1	0	X
1	1	1	0	1	1	X
1	1	1	1	0	0	X
1	1	1	1	0	1	X
1	1	1	1	1	0	X
1	1	1	1	1	1	X
*/
