// Digital circuit displayP.dig as structural Verilog
module displayP (
  input  Q1,
  input  Q2,
  output b,
  output d,
  output e,
  output g,
  output f,
  output c,
  output a
);

  not not_1 (a, Q1);
  not not_2 (c, Q2);
  xnor xnor_1 (f, Q2, Q1);

  assign b = 1'b1;
  assign d = a;
  assign e = a;
  assign g = Q2;
endmodule

/* Test case:
Q2	Q1	a	d 	e 	b 	c 	f 	g
0 	0 	1 	1	1 	1	1	1	0
0	1 	0 	0	0	1	1	0	0	
1 	0 	1 	1 	1	1	0	0	1
1	1 	x 	x 	x 	x 	x	x	x
*/
