// Digital circuit solucio.dig as structural Verilog
module solucio (
  input  X0,
  input  X1,
  input  X2,
  input  CLK,
  output Q1,
  output Q2,
  output M,
  output Q0,
  output P1,
  output P0
);

  wire and_2_out, d0_1_d0, d1_1_d1, d2_1_d2, displayp_1_a, displayp_1_b, displayp_1_c, displayp_1_d,
       displayp_1_e, displayp_1_f, displayp_1_g, not_1_out, not_2_out, not_3_out, not_4_out, not_5_out,
       not_6_out, not_7_out;

  or or_1 (P1, and_2_out, X1);
  and and_1 (P0, not_5_out, not_1_out);
  and and_2 (and_2_out, not_6_out, not_5_out);
  Motor motor_1 (.X0(X0), .X1(X1), .X2(X2), .Q0(Q0), .Q1(Q1), .Q2(Q2), .M(M));
  not not_1 (not_1_out, X0);
  not not_2 (not_2_out, X1);
  not not_3 (not_3_out, X2);
  not not_4 (not_4_out, Q0);
  not not_5 (not_5_out, Q1);
  not not_6 (not_6_out, Q2);
  D0 d0_1 (.X0(X0), .X1(X1), .X2(X2), .Q0(Q0), .D0(d0_1_d0));
  D1 d1_1 (.X0(X0), .X1(X1), .X2(X2), .Q1(Q1), .D1(d1_1_d1));
  D2 d2_1 (.X0(X0), .X1(X1), .X2(X2), .Q2(Q2), .D2(d2_1_d2));
  D_FF D0_2 (.D(d0_1_d0), .C(CLK), .Q(Q0));  // open: nQ
  D_FF D1_2 (.D(d1_1_d1), .C(CLK), .Q(Q1));  // open: nQ
  D_FF D2_2 (.D(d2_1_d2), .C(CLK), .Q(Q2));  // open: nQ
  not not_7 (not_7_out, Q0);
  displayP displayp_1 (
    .Q1(Q1), .Q2(Q2), .a(displayp_1_a), .b(displayp_1_b), .c(displayp_1_c), .d(displayp_1_d),
    .e(displayp_1_e), .f(displayp_1_f), .g(displayp_1_g));
  Seven_Seg seven_seg_1 (
    .a(not_7_out), .b(1'b1), .c(1'b1), .d(not_7_out), .e(not_7_out), .f(not_7_out), .g(1'b0), .dp(1'b0));
  Seven_Seg seven_seg_2 (
    .a(displayp_1_a), .b(displayp_1_b), .c(displayp_1_c), .d(displayp_1_d), .e(displayp_1_e),
    .f(displayp_1_f), .g(displayp_1_g), .dp(1'b0));

  // Notes on the sheet:
  //   Q0
  //   Q1
  //   Q2
  //   Caja
  //   Planta actual
endmodule

/* Test case T1:
X2	X1	X0	Q2	Q1	Q0	P1	P0	M	CLK
0	0	0	0	0	0	X	X	0	0
0	0	1	0	0	0	1	0	1	0
0	1	0	0	0	0	1	1	1	0
0	1	1	0	0	0	X	X	0	0
1	0	0	0	0	0	X	X	0	0
1	0	1	0	0	0	X	X	0	0
1	1	0	0	0	0	X	X	0	0
1	1	1	0	0	0	X	X	0	0
0	1	1	0	0	1	x	x	0	c
0	0	0	0	0	1	X	X	0	0
0	0	1	0	0	1	1	0	1	0
0	1	0	0	0	1	1	1	1	0
0	1	1	0	0	1	X	X	0	0
1	0	0	0	0	1	X	X	0	0
1	0	1	0	0	1	X	X	0	0
1	1	0	0	0	1	X	X	0	0
1	1	1	0	0	1	X	X	0	0
0	0	1	0	1	1	x	x	0	c
1	0	0	0	1	0	x	x	0	c
0	0	0	0	1	0	0	0	1	0
0	0	1	0	1	0	X	X	0	0
0	1	0	0	1	0	1	0	1	0
0	1	1	0	1	0	X	X	0	0
1	0	0	0	1	0	X	X	0	0
1	0	1	0	1	0	X	X	0	0
1	1	0	0	1	0	X	X	0	0
1	1	1	0	1	0	X	X	0	0
0	1	1	0	1	1	x	x	0	c
0	0	0	0	1	1	0	0	1	0
0	0	1	0	1	1	X	X	0	0
0	1	0	0	1	1	1	0	1	0
0	1	1	0	1	1	X	X	0	0
1	0	0	0	1	1	X	X	0	0
1	0	1	0	1	1	X	X	0	0
1	1	0	0	1	1	X	X	0	0
1	1	1	0	1	1	X	X	0	0
0	1	0	1	0	1	x	x	0	c
1	0	0	1	0	0	x	x	0	c
0	0	0	1	0	0	0	1	1	0
0	0	1	1	0	0	0	0	1	0
0	1	0	1	0	0	X	X	0	0
0	1	1	1	0	0	X	X	0	0
1	0	0	1	0	0	X	X	0	0
1	0	1	1	0	0	X	X	0	0
1	1	0	1	0	0	X	X	0	0
1	1	1	1	0	0	X	X	0	0
0	1	1	1	0	1	x	x	0	c
0	0	0	1	0	1	0	1	1	0
0	0	1	1	0	1	0	0	1	0
0	1	0	1	0	1	X	X	0	0
0	1	1	1	0	1	X	X	0	0
1	0	0	1	0	1	X	X	0	0
1	0	1	1	0	1	X	X	0	0
1	1	0	1	0	1	X	X	0	0
1	1	1	1	0	1	X	X	0	0
*/

/* Test case T2:
CLK	X2	X1	X0	Q2	Q1	Q0	P1	P0	M
0	1	1	1	0	0	0	x	x	0
c	0	0	1	0	1	0	0	0	0
c	0	1	0	1	0	0	1	1	0
c	0	0	0	0	0	0	x	x	0
c	0	1	1	0	0	1	x	x	0
c	0	0	0	0	0	1	x	x	0
c	0	1	0	1	0	1	1	1	0
c	0	0	1	0	1	1	0	0	0
c	1	0	0	0	1	0	x	x	0
c	0	1	0	1	0	0	1	1	0
c	1	1	0	1	0	0	x	x	0
c	1	0	0	1	0	0	x	x	0
c	0	0	1	0	1	0	0	0	0
c	0	1	1	0	1	1	x	x	0
c	0	1	0	1	0	1	x	1	0
c	0	0	0	0	0	1	x	1	0
c	1	1	0	0	0	1	x	x	0
c	0	1	1	0	0	1	x	x	0
c	1	1	1	0	0	1	x	x	0
c	0	1	0	1	0	1	x	x	0
c	0	0	0	0	0	1	x	x	0
c	0	0	1	0	1	1	x	x	0
c	0	1	1	0	1	1	x	x	0
c	1	1	0	0	1	1	x	x	0
c	1	0	0	0	1	0	x	x	0
c	0	1	0	1	0	0	x	x	0
c	0	1	1	1	0	1	x	x	0
c	0	1	1	1	0	1	x	x	0
c	0	0	1	0	1	1	x	x	0
c	1	1	0	0	1	1	x	x	0
c	0	0	0	0	0	1	x	x	0
c	0	1	1	0	0	1	x	x	0
c	1	0	0	0	0	0	x	x	0
c	1	0	0	0	0	0	x	x	0
c	1	1	0	0	0	0	x	x	0
c	1	0	1	0	0	0	x	x	0
c	0	0	1	0	1	0	x	x	0
c	0	1	1	0	1	1	x	x	0
c	0	1	1	0	1	1	x	x	0
c	0	1	0	1	0	1	x	x	0
c	1	0	0	1	0	0	x	x	0
c	0	0	0	0	0	0	x	x	0
c	0	1	0	1	0	0	x	x	0
c	1	0	0	1	0	0	x	x	0
c	0	0	1	0	1	0	x	x	0
c	1	1	1	0	1	0	x	x	0
c	1	0	1	0	1	0	x	x	0
c	0	1	1	0	1	1	x	x	0
c	1	1	0	0	1	1	x	x	0
c	0	1	1	0	1	1	x	x	0
c	0	0	0	0	0	1	x	x	0
c	0	1	0	1	0	1	x	x	0
c	0	0	0	0	0	1	x	x	0
c	1	0	0	0	0	0	x	x	0
*/
